// Logisim project KnockUnlockSchematic.circ as structural Verilog: 1 circuit, main circuit KnockUnlock
module KnockUnlock (
  input  Power_Supply__V,
  input  Power_Supply__V_2,
  input  Arduino__V,
  output Motor__V,
  output Motor__V_2
);

  Transistor transistor_1 ();  // open: in, out, gate
endmodule
